// Logisim project Organizacion_computadores_JCS.circ as structural Verilog
module NAND (
  input  A,
  input  B,
  output OUT
);

  wire and_1_out;

  and and_1 (and_1_out, A, A, B);
  not not_1 (OUT, and_1_out);
endmodule

module NOT (
  input  A,
  output out_2
);

  NAND nand_1 (.A(A), .B(A), .OUT(out_2));
endmodule

module XOR (
  input  A,
  input  B,
  output out_3
);

  wire and_1_out_3, and_2_out_3, not_1_out_2, not_2_out_2;

  NOT not_1 (.A(A), .out_2(not_1_out_2));
  NOT not_2 (.A(B), .out_2(not_2_out_2));
  AND and_1 (.in_1(not_1_out_2), .in_2(B), .out_3(and_1_out_3));
  AND and_2 (.in_1(A), .in_2(not_2_out_2), .out_3(and_2_out_3));
  OR or_1 (.A(and_1_out_3), .B(and_2_out_3), .out_3(out_3));
endmodule

module AND (
  input  in_1,
  input  in_2,
  output out_3
);

  wire nand_1_out;

  NAND nand_1 (.A(in_1), .B(in_2), .OUT(nand_1_out));
  NOT not_1 (.A(nand_1_out), .out_2(out_3));
endmodule

module OR (
  input  A,
  input  B,
  output out_3
);

  wire not_1_out_2, not_2_out_2;

  NOT not_1 (.A(A), .out_2(not_1_out_2));
  NOT not_2 (.A(B), .out_2(not_2_out_2));
  NAND nand_1 (.A(not_1_out_2), .B(not_2_out_2), .OUT(out_3));
endmodule

module MUX (
  input  A,
  input  B,
  input  SEL,
  output out_4
);

  wire and_1_out_3, and_2_out_3, not_1_out_2;

  NOT not_1 (.A(SEL), .out_2(not_1_out_2));
  AND and_1 (.in_1(A), .in_2(not_1_out_2), .out_3(and_1_out_3));
  AND and_2 (.in_1(B), .in_2(SEL), .out_3(and_2_out_3));
  OR or_1 (.A(and_1_out_3), .B(and_2_out_3), .out_3(out_4));
endmodule

module DMUX (
  input  IN,
  input  SEL,
  output Y0,
  output Y1
);

  wire not_1_out_2;

  NOT not_1 (.A(SEL), .out_2(not_1_out_2));
  AND and_1 (.in_1(IN), .in_2(not_1_out_2), .out_3(Y0));
  AND and_2 (.in_1(IN), .in_2(SEL), .out_3(Y1));
endmodule

module NOT16 (
  input  [15:0] in_1,
  output [15:0] out_2
);

  assign out_2 = ~in_1;  // NOT_Gate not_1, 16 bits wide
endmodule

module AND16 (
  input  [15:0] A,
  input  [15:0] B,
  output [15:0] out_3
);

  assign out_3 = A & B;  // AND_Gate and_1, 16 bits wide
endmodule

module OR16 (
  input  [15:0] A,
  input  [15:0] B,
  output [15:0] out_3
);

  assign out_3 = A | B;  // OR_Gate or_1, 16 bits wide
endmodule

// HADD
module SUMADOR_BINARIO (
  input  A,
  input  B,
  output out_3,
  output out_4
);

  xor XOR (out_3, A, B);
  and AND (out_4, A, B);
endmodule

// FADD
module SUMADOR_BINARIO_COMPLETO (
  input  A,
  input  B,
  input  CARRY_IN,
  output out_4,
  output out_5
);

  wire AND_2_out, AND_out, XOR_out;

  xor XOR (XOR_out, A, B);
  and AND (AND_out, A, B);
  xor XOR_2 (out_4, XOR_out, CARRY_IN);
  and AND_2 (AND_2_out, XOR_out, CARRY_IN);
  or OR (out_5, AND_out, AND_2_out);
endmodule

module PRUEBA_DEL_RELOJ (
  input  IN,
  input  LOAD,
  output OUT
);

  wire clock_1_out;

  Clock clock_1 (.out(clock_1_out));
  D_Flip_Flop d_ff_1 (.clk(clock_1_out), .D(IN), .Q(OUT), .en(LOAD));  // open: Qn, preset, reset
endmodule

module REGISTRO_1_BIT (
  input  IN,
  input  LOAD,
  output out_3
);

  wire clock_1_out, mux_1_out_4;

  MUX mux_1 (.A(out_3), .B(IN), .SEL(LOAD), .out_4(mux_1_out_4));
  Clock clock_1 (.out(clock_1_out));
  D_Flip_Flop d_ff_1 (.clk(clock_1_out), .D(mux_1_out_4), .Q(out_3));  // open: Qn, preset, en, reset
endmodule

module REGISTRO (
  input  [15:0] IN,
  input  LOAD,
  output [15:0] out_3
);

  REGISTRO_1_BIT registro_1_bit_1 (.IN(IN[0]), .LOAD(LOAD), .out_3(out_3[0]));
  REGISTRO_1_BIT registro_1_bit_2 (.IN(IN[1]), .LOAD(LOAD), .out_3(out_3[1]));
  REGISTRO_1_BIT registro_1_bit_3 (.IN(IN[2]), .LOAD(LOAD), .out_3(out_3[2]));
  REGISTRO_1_BIT registro_1_bit_4 (.IN(IN[3]), .LOAD(LOAD), .out_3(out_3[3]));
  REGISTRO_1_BIT registro_1_bit_5 (.IN(IN[4]), .LOAD(LOAD), .out_3(out_3[4]));
  REGISTRO_1_BIT registro_1_bit_6 (.IN(IN[5]), .LOAD(LOAD), .out_3(out_3[5]));
  REGISTRO_1_BIT registro_1_bit_7 (.IN(IN[6]), .LOAD(LOAD), .out_3(out_3[6]));
  REGISTRO_1_BIT registro_1_bit_8 (.IN(IN[7]), .LOAD(LOAD), .out_3(out_3[7]));
  REGISTRO_1_BIT registro_1_bit_9 (.IN(IN[8]), .LOAD(LOAD), .out_3(out_3[8]));
  REGISTRO_1_BIT registro_1_bit_10 (.IN(IN[9]), .LOAD(LOAD), .out_3(out_3[9]));
  REGISTRO_1_BIT registro_1_bit_11 (.IN(IN[10]), .LOAD(LOAD), .out_3(out_3[10]));
  REGISTRO_1_BIT registro_1_bit_12 (.IN(IN[11]), .LOAD(LOAD), .out_3(out_3[11]));
  REGISTRO_1_BIT registro_1_bit_13 (.IN(IN[12]), .LOAD(LOAD), .out_3(out_3[12]));
  REGISTRO_1_BIT registro_1_bit_14 (.IN(IN[13]), .LOAD(LOAD), .out_3(out_3[13]));
  REGISTRO_1_BIT registro_1_bit_15 (.IN(IN[14]), .LOAD(LOAD), .out_3(out_3[14]));
  REGISTRO_1_BIT registro_1_bit_16 (.IN(IN[15]), .LOAD(LOAD), .out_3(out_3[15]));
endmodule

module MUX16 (
  input  [15:0] A,
  input  [15:0] B,
  input  SEL,
  output [15:0] OUT
);

  Multiplexer #(.width(16)) multiplexer_1 (.in0(A), .in1(B), .out(OUT), .sel(SEL));  // open: en
endmodule

module OR8WAY (
  input  [7:0] IN,
  output out_2
);

  or OR (out_2, IN[0], IN[1], IN[2], IN[3], IN[4], IN[5], IN[6], IN[7]);
endmodule

module MUX4WAY16 (
  input  [15:0] A,
  input  [15:0] B,
  input  [15:0] C,
  input  [15:0] D,
  input  [1:0] SEL,
  output [15:0] OUT
);

  Multiplexer #(.select(2), .width(16)) multiplexer_1 (
    .in0(A), .in1(B), .in2(C), .in3(D), .out(OUT), .sel(SEL));  // open: en
endmodule

module MUX8WAY16 (
  input  [15:0] A,
  input  [15:0] B,
  input  [15:0] C,
  input  [15:0] D,
  input  [15:0] E,
  input  [15:0] F,
  input  [15:0] G,
  input  [15:0] H,
  input  [2:0] SEL,
  output [15:0] OUT
);

  Multiplexer #(.select(3), .width(16)) multiplexer_1 (
    .in0(A), .in1(B), .in2(C), .in3(D), .in4(E), .in5(F), .in6(G), .in7(H), .out(OUT), .sel(SEL));  // open: en
endmodule

module DMUX4WAY (
  input  IN,
  input  [1:0] SEL,
  output A,
  output B,
  output C,
  output D
);

  Demultiplexer #(.select(2)) demultiplexer_1 (.out0(A), .out1(B), .out2(C), .out3(D), .in(IN), .sel(SEL));  // open: en
endmodule

module DMUX8WAY (
  input  IN,
  input  [2:0] SEL,
  output A,
  output B,
  output C,
  output D,
  output E,
  output F,
  output G,
  output H
);

  Demultiplexer #(.select(3)) demultiplexer_1 (
    .out0(A), .out1(B), .out2(C), .out3(D), .out4(E), .out5(F), .out6(G), .out7(H), .in(IN), .sel(SEL));  // open: en
endmodule

module ADD16 (
  input  [15:0] A,
  input  [15:0] B,
  output [15:0] OUT
);

  wire sumador_binario_completo_1_out_5, sumador_binario_completo_2_out_5, sumador_binario_completo_3_out_5,
       sumador_binario_completo_4_out_5, sumador_binario_completo_5_out_5, sumador_binario_completo_6_out_5,
       sumador_binario_completo_7_out_5, sumador_binario_completo_8_out_5, sumador_binario_completo_9_out_5,
       sumador_binario_completo_10_out_5, sumador_binario_completo_11_out_5,
       sumador_binario_completo_12_out_5, sumador_binario_completo_13_out_5,
       sumador_binario_completo_14_out_5, sumador_binario_completo_15_out_5;

  SUMADOR_BINARIO_COMPLETO sumador_binario_completo_1 (
    .A(A[0]), .B(B[0]), .out_4(OUT[0]), .out_5(sumador_binario_completo_1_out_5));  // open: CARRY_IN
  SUMADOR_BINARIO_COMPLETO sumador_binario_completo_2 (
    .A(A[1]), .B(B[1]), .CARRY_IN(sumador_binario_completo_1_out_5), .out_4(OUT[1]),
    .out_5(sumador_binario_completo_2_out_5));
  SUMADOR_BINARIO_COMPLETO sumador_binario_completo_3 (
    .A(A[2]), .B(B[2]), .CARRY_IN(sumador_binario_completo_2_out_5), .out_4(OUT[2]),
    .out_5(sumador_binario_completo_3_out_5));
  SUMADOR_BINARIO_COMPLETO sumador_binario_completo_4 (
    .A(A[3]), .B(B[3]), .CARRY_IN(sumador_binario_completo_3_out_5), .out_4(OUT[3]),
    .out_5(sumador_binario_completo_4_out_5));
  SUMADOR_BINARIO_COMPLETO sumador_binario_completo_5 (
    .A(A[4]), .B(B[4]), .CARRY_IN(sumador_binario_completo_4_out_5), .out_4(OUT[4]),
    .out_5(sumador_binario_completo_5_out_5));
  SUMADOR_BINARIO_COMPLETO sumador_binario_completo_6 (
    .A(A[5]), .B(B[5]), .CARRY_IN(sumador_binario_completo_5_out_5), .out_4(OUT[5]),
    .out_5(sumador_binario_completo_6_out_5));
  SUMADOR_BINARIO_COMPLETO sumador_binario_completo_7 (
    .A(A[6]), .B(B[6]), .CARRY_IN(sumador_binario_completo_6_out_5), .out_4(OUT[6]),
    .out_5(sumador_binario_completo_7_out_5));
  SUMADOR_BINARIO_COMPLETO sumador_binario_completo_8 (
    .A(A[7]), .B(B[7]), .CARRY_IN(sumador_binario_completo_7_out_5), .out_4(OUT[7]),
    .out_5(sumador_binario_completo_8_out_5));
  SUMADOR_BINARIO_COMPLETO sumador_binario_completo_9 (
    .A(A[8]), .B(B[8]), .CARRY_IN(sumador_binario_completo_8_out_5), .out_4(OUT[8]),
    .out_5(sumador_binario_completo_9_out_5));
  SUMADOR_BINARIO_COMPLETO sumador_binario_completo_10 (
    .A(A[9]), .B(B[9]), .CARRY_IN(sumador_binario_completo_9_out_5), .out_4(OUT[9]),
    .out_5(sumador_binario_completo_10_out_5));
  SUMADOR_BINARIO_COMPLETO sumador_binario_completo_11 (
    .A(A[10]), .B(B[10]), .CARRY_IN(sumador_binario_completo_10_out_5), .out_4(OUT[10]),
    .out_5(sumador_binario_completo_11_out_5));
  SUMADOR_BINARIO_COMPLETO sumador_binario_completo_12 (
    .A(A[11]), .B(B[11]), .CARRY_IN(sumador_binario_completo_11_out_5), .out_4(OUT[11]),
    .out_5(sumador_binario_completo_12_out_5));
  SUMADOR_BINARIO_COMPLETO sumador_binario_completo_13 (
    .A(A[12]), .B(B[12]), .CARRY_IN(sumador_binario_completo_12_out_5), .out_4(OUT[12]),
    .out_5(sumador_binario_completo_13_out_5));
  SUMADOR_BINARIO_COMPLETO sumador_binario_completo_14 (
    .A(A[13]), .B(B[13]), .CARRY_IN(sumador_binario_completo_13_out_5), .out_4(OUT[13]),
    .out_5(sumador_binario_completo_14_out_5));
  SUMADOR_BINARIO_COMPLETO sumador_binario_completo_15 (
    .A(A[14]), .B(B[14]), .CARRY_IN(sumador_binario_completo_14_out_5), .out_4(OUT[14]),
    .out_5(sumador_binario_completo_15_out_5));
  SUMADOR_BINARIO_COMPLETO sumador_binario_completo_16 (
    .A(A[15]), .B(B[15]), .CARRY_IN(sumador_binario_completo_15_out_5), .out_4(OUT[15]));  // open: out_5
endmodule

module INC16 (
  input  [15:0] A,
  output [15:0] OUT
);

  ADD16 add16_1 (.A(A), .B(16'h1), .OUT(OUT));
endmodule

module ALU (
  input  [15:0] X,
  input  ZX,
  input  NX,
  input  F,
  input  [15:0] Y,
  input  ZY,
  input  NY,
  input  NO,
  output [15:0] OUT,
  output ZR,
  output NG
);

  wire or_1_out;
  wire [15:0] add16_1_out, and_1_out, multiplexer_1_out, multiplexer_2_out, multiplexer_4_out,
       multiplexer_5_out, multiplexer_6_out, not_1_out, not_2_out, not_3_out;

  assign not_1_out = ~multiplexer_6_out;  // NOT_Gate not_1, 16 bits wide
  Multiplexer #(.width(16)) multiplexer_1 (.in0(X), .in1({16{1'b0}}), .out(multiplexer_1_out), .sel(ZX));  // open: en
  Multiplexer #(.width(16)) multiplexer_2 (.in0(Y), .in1({16{1'b0}}), .out(multiplexer_2_out), .sel(ZY));  // open: en
  Multiplexer #(.width(16)) multiplexer_3 (
    .in0(multiplexer_6_out), .in1(not_1_out), .out({NG, OUT[14:0]}), .sel(NO));  // open: en
  assign not_2_out = ~multiplexer_1_out;  // NOT_Gate not_2, 16 bits wide
  assign not_3_out = ~multiplexer_2_out;  // NOT_Gate not_3, 16 bits wide
  Multiplexer #(.width(16)) multiplexer_4 (
    .in0(multiplexer_1_out), .in1(not_2_out), .out(multiplexer_4_out), .sel(NX));  // open: en
  Multiplexer #(.width(16)) multiplexer_5 (
    .in0(multiplexer_2_out), .in1(not_3_out), .out(multiplexer_5_out), .sel(NY));  // open: en
  assign and_1_out = multiplexer_4_out & multiplexer_5_out;  // AND_Gate and_1, 16 bits wide
  or or_1 (or_1_out, OUT[0], OUT[1], OUT[2], OUT[3], OUT[4], OUT[5], OUT[6], OUT[7], OUT[8], OUT[9], OUT[10], OUT[11], OUT[12], OUT[13], OUT[14], NG);
  ADD16 add16_1 (.A(multiplexer_4_out), .B(multiplexer_5_out), .OUT(add16_1_out));
  not not_4 (ZR, or_1_out);
  Multiplexer #(.width(16)) multiplexer_6 (
    .in0(and_1_out), .in1(add16_1_out), .out(multiplexer_6_out), .sel(F));  // open: en

  assign OUT[15] = NG;
endmodule
